// Logisim project Alu.circ as structural Verilog: 3 circuits, main circuit main
module main (
);

  wire [31:0] undriven;

  ALu alu_1 (.in_1(undriven));  // open: in_2, Zero, in_3, out_5
endmodule

module ALu (
  input  [31:0] in_1,
  input  [31:0] in_2,
  input  [3:0] in_3,
  output Zero,
  output [31:0] out_5
);

  wire comparator_1_lt;
  wire [31:0] adder_1_out, and_1_out, extensor_1_out_2, nor_1_out, or_1_out, subtractor_1_out;

  Comparator #(.width(32)) comparator_1 (.a(in_1), .b(in_2), .eq(Zero), .lt(comparator_1_lt));  // open: gt
  Adder #(.width(32)) adder_1 (.a(in_1), .b(in_2), .out(adder_1_out));  // open: cin, cout
  Subtractor #(.width(32)) subtractor_1 (.a(in_1), .b(in_2), .out(subtractor_1_out));  // open: bin, bout
  Extensor extensor_1 (.in_1(comparator_1_lt), .out_2(extensor_1_out_2));
  assign and_1_out = in_1 & in_2;  // AND_Gate and_1, 32 bits wide
  assign or_1_out = in_1 | in_2;  // OR_Gate or_1, 32 bits wide
  assign nor_1_out = ~(in_1 | in_2);  // NOR_Gate nor_1, 32 bits wide
  Multiplexer #(.select(4), .width(32)) multiplexer_1 (
    .in0(and_1_out), .in1(or_1_out), .in2(adder_1_out), .in6(subtractor_1_out), .in7(extensor_1_out_2),
    .in12(nor_1_out), .out(out_5), .sel(in_3));  // open: in3, in4, in5, in8, in9, in10, in11, in13, in14, in15, en
endmodule

module Extensor (
  input  in_1,
  output [31:0] out_2
);


  assign out_2 = {in_1, {31{1'b0}}};
endmodule
