// Logisim project BancoRegistros.circ as structural Verilog: 4 circuits, main circuit main
module main (
  input  [4:0] Read_registro__1,
  input  [4:0] Read_registro__2,
  input  [4:0] Registro_a_guardar,
  input  Enable,
  input  [31:0] in_5,
  input  in_6,
  input  in_7,
  input  in_8,
  output [31:0] Read_data1,
  output [31:0] Read_data2
);

  wire clock_1_out;

  D_Flip_Flop d_ff_1 (.clk(in_6), .D(in_7), .en(in_8));  // open: Q, Qn, preset, reset
  Clock clock_1 (.out(clock_1_out));
  // Banco banco_1: pin names not known; wires that end beside it: Enable, clock_1_out, Read_data1, Read_data2
endmodule

module Registro_32bits (
  input  CLock,
  input  Enable,
  input  [31:0] in_3,
  output [31:0] out_4
);

  D_Flip_Flop d_ff_1 (.clk(CLock), .D(in_3[0]), .Q(out_4[0]), .en(Enable));  // open: Qn, preset, reset
  D_Flip_Flop d_ff_2 (.clk(CLock), .D(in_3[8]), .Q(out_4[8]), .en(Enable));  // open: Qn, preset, reset
  D_Flip_Flop d_ff_3 (.clk(CLock), .D(in_3[16]), .Q(out_4[16]), .en(Enable));  // open: Qn, preset, reset
  D_Flip_Flop d_ff_4 (.clk(CLock), .D(in_3[24]), .Q(out_4[24]), .en(Enable));  // open: Qn, preset, reset
  D_Flip_Flop d_ff_5 (.clk(CLock), .D(in_3[1]), .Q(out_4[1]), .en(Enable));  // open: Qn, preset, reset
  D_Flip_Flop d_ff_6 (.clk(CLock), .D(in_3[9]), .Q(out_4[9]), .en(Enable));  // open: Qn, preset, reset
  D_Flip_Flop d_ff_7 (.clk(CLock), .D(in_3[17]), .Q(out_4[17]), .en(Enable));  // open: Qn, preset, reset
  D_Flip_Flop d_ff_8 (.clk(CLock), .D(in_3[25]), .Q(out_4[25]), .en(Enable));  // open: Qn, preset, reset
  D_Flip_Flop d_ff_9 (.clk(CLock), .D(in_3[2]), .Q(out_4[2]), .en(Enable));  // open: Qn, preset, reset
  D_Flip_Flop d_ff_10 (.clk(CLock), .D(in_3[10]), .Q(out_4[10]), .en(Enable));  // open: Qn, preset, reset
  D_Flip_Flop d_ff_11 (.clk(CLock), .D(in_3[18]), .Q(out_4[18]), .en(Enable));  // open: Qn, preset, reset
  D_Flip_Flop d_ff_12 (.clk(CLock), .D(in_3[26]), .Q(out_4[26]), .en(Enable));  // open: Qn, preset, reset
  D_Flip_Flop d_ff_13 (.clk(CLock), .D(in_3[3]), .Q(out_4[3]), .en(Enable));  // open: Qn, preset, reset
  D_Flip_Flop d_ff_14 (.clk(CLock), .D(in_3[11]), .Q(out_4[11]), .en(Enable));  // open: Qn, preset, reset
  D_Flip_Flop d_ff_15 (.clk(CLock), .D(in_3[19]), .Q(out_4[19]), .en(Enable));  // open: Qn, preset, reset
  D_Flip_Flop d_ff_16 (.clk(CLock), .D(in_3[27]), .Q(out_4[27]), .en(Enable));  // open: Qn, preset, reset
  D_Flip_Flop d_ff_17 (.clk(CLock), .D(in_3[4]), .Q(out_4[4]), .en(Enable));  // open: Qn, preset, reset
  D_Flip_Flop d_ff_18 (.clk(CLock), .D(in_3[12]), .Q(out_4[12]), .en(Enable));  // open: Qn, preset, reset
  D_Flip_Flop d_ff_19 (.clk(CLock), .D(in_3[20]), .Q(out_4[20]), .en(Enable));  // open: Qn, preset, reset
  D_Flip_Flop d_ff_20 (.clk(CLock), .D(in_3[28]), .Q(out_4[28]), .en(Enable));  // open: Qn, preset, reset
  D_Flip_Flop d_ff_21 (.clk(CLock), .D(in_3[5]), .Q(out_4[5]), .en(Enable));  // open: Qn, preset, reset
  D_Flip_Flop d_ff_22 (.clk(CLock), .D(in_3[13]), .Q(out_4[13]), .en(Enable));  // open: Qn, preset, reset
  D_Flip_Flop d_ff_23 (.clk(CLock), .D(in_3[21]), .Q(out_4[21]), .en(Enable));  // open: Qn, preset, reset
  D_Flip_Flop d_ff_24 (.clk(CLock), .D(in_3[29]), .Q(out_4[29]), .en(Enable));  // open: Qn, preset, reset
  D_Flip_Flop d_ff_25 (.clk(CLock), .D(in_3[6]), .Q(out_4[6]), .en(Enable));  // open: Qn, preset, reset
  D_Flip_Flop d_ff_26 (.clk(CLock), .D(in_3[14]), .Q(out_4[14]), .en(Enable));  // open: Qn, preset, reset
  D_Flip_Flop d_ff_27 (.clk(CLock), .D(in_3[22]), .Q(out_4[22]), .en(Enable));  // open: Qn, preset, reset
  D_Flip_Flop d_ff_28 (.clk(CLock), .D(in_3[30]), .Q(out_4[30]), .en(Enable));  // open: Qn, preset, reset
  D_Flip_Flop d_ff_29 (.clk(CLock), .D(in_3[7]), .Q(out_4[7]), .en(Enable));  // open: Qn, preset, reset
  D_Flip_Flop d_ff_30 (.clk(CLock), .D(in_3[15]), .Q(out_4[15]), .en(Enable));  // open: Qn, preset, reset
  D_Flip_Flop d_ff_31 (.clk(CLock), .D(in_3[23]), .Q(out_4[23]), .en(Enable));  // open: Qn, preset, reset
  D_Flip_Flop d_ff_32 (.clk(CLock), .D(in_3[31]), .Q(out_4[31]), .en(Enable));  // open: Qn, preset, reset
endmodule

module _8x32 (
  input  Enable,
  input  [2:0] Selec_Salida,
  input  Clock,
  input  [31:0] in_4,
  input  [2:0] Mux2,
  input  [2:0] Mux1,
  output [31:0] Salida_1,
  output [31:0] out_8
);

  wire decoder_1_out0, decoder_1_out1, decoder_1_out2, decoder_1_out3, decoder_1_out4, decoder_1_out5,
       decoder_1_out6, decoder_1_out7;
  wire [31:0] _0_out_4, _1_out_4, _2_out_4, _3_out_4, _4_out_4, _5_out_4, _6_out_4, _7_out_4,
       demultiplexer_1_out0, demultiplexer_1_out1, demultiplexer_1_out2, demultiplexer_1_out3,
       demultiplexer_1_out4, demultiplexer_1_out5, demultiplexer_1_out6, demultiplexer_1_out7;

  Demultiplexer #(.select(3), .width(32), .enable("false")) demultiplexer_1 (
    .out0(demultiplexer_1_out0), .out1(demultiplexer_1_out1), .out2(demultiplexer_1_out2),
    .out3(demultiplexer_1_out3), .out4(demultiplexer_1_out4), .out5(demultiplexer_1_out5),
    .out6(demultiplexer_1_out6), .out7(demultiplexer_1_out7), .in(in_4), .sel(Selec_Salida));
  Registro_32bits _0 (.CLock(Clock), .Enable(decoder_1_out0), .in_3(demultiplexer_1_out0), .out_4(_0_out_4));
  Registro_32bits _4 (.CLock(Clock), .Enable(decoder_1_out4), .in_3(demultiplexer_1_out4), .out_4(_4_out_4));
  Decoder #(.select(3), .disabled(0)) decoder_1 (
    .out0(decoder_1_out0), .out1(decoder_1_out1), .out2(decoder_1_out2), .out3(decoder_1_out3),
    .out4(decoder_1_out4), .out5(decoder_1_out5), .out6(decoder_1_out6), .out7(decoder_1_out7),
    .sel(Selec_Salida), .en(Enable));
  Registro_32bits _1 (.CLock(Clock), .Enable(decoder_1_out1), .in_3(demultiplexer_1_out1), .out_4(_1_out_4));
  Registro_32bits _5 (.CLock(Clock), .Enable(decoder_1_out5), .in_3(demultiplexer_1_out5), .out_4(_5_out_4));
  Registro_32bits _2 (.CLock(Clock), .Enable(decoder_1_out2), .in_3(demultiplexer_1_out2), .out_4(_2_out_4));
  Registro_32bits _6 (.CLock(Clock), .Enable(decoder_1_out6), .in_3(demultiplexer_1_out6), .out_4(_6_out_4));
  Registro_32bits _3 (.CLock(Clock), .Enable(decoder_1_out3), .in_3(demultiplexer_1_out3), .out_4(_3_out_4));
  Registro_32bits _7 (.CLock(Clock), .Enable(decoder_1_out7), .in_3(demultiplexer_1_out7), .out_4(_7_out_4));
  Multiplexer #(.select(3), .width(32), .enable("false")) multiplexer_1 (
    .in0(_0_out_4), .in1(_1_out_4), .in2(_2_out_4), .in3(_3_out_4), .in4(_4_out_4), .in5(_5_out_4),
    .in6(_6_out_4), .in7(_7_out_4), .out(Salida_1), .sel(Mux1));
  Multiplexer #(.select(3), .width(32), .enable("false")) multiplexer_2 (
    .in0(_0_out_4), .in1(_1_out_4), .in2(_2_out_4), .in3(_3_out_4), .in4(_4_out_4), .in5(_5_out_4),
    .in6(_6_out_4), .in7(_7_out_4), .out(out_8), .sel(Mux2));
endmodule

// Banco registros
module Banco (
  input  Enable,
  input  Clock,
  input  [4:0] Read_1,
  input  [4:0] Read_2,
  input  [4:0] Select_Registro,
  input  [31:0] in_6,
  output [31:0] out_7,
  output [31:0] out_8
);

  wire and_1_out, decoder_1_out0, decoder_1_out1, decoder_1_out2, decoder_1_out3, or_1_out;
  wire [31:0] demultiplexer_1_out0, demultiplexer_1_out1, demultiplexer_1_out2, demultiplexer_1_out3,
       n8x32_1_out_8, n8x32_1_salida_1, n8x32_2_out_8, n8x32_2_salida_1, n8x32_3_out_8, n8x32_3_salida_1,
       n8x32_4_out_8, n8x32_4_salida_1;

  or or_1 (or_1_out, Select_Registro[4], Select_Registro[3], Select_Registro[2], Select_Registro[1], Select_Registro[0]);
  Demultiplexer #(.select(2), .width(32), .enable("false")) demultiplexer_1 (
    .out0(demultiplexer_1_out0), .out1(demultiplexer_1_out1), .out2(demultiplexer_1_out2),
    .out3(demultiplexer_1_out3), .in(in_6), .sel({Select_Registro[3], Select_Registro[4]}));
  and and_1 (and_1_out, or_1_out, Enable);
  _8x32 u_8x32_1 (
    .Enable(decoder_1_out0), .Selec_Salida({Select_Registro[0], Select_Registro[1], Select_Registro[2]}),
    .Clock(Clock), .in_4(demultiplexer_1_out0), .Salida_1(n8x32_1_salida_1), .out_8(n8x32_1_out_8),
    .Mux2({Read_2[0], Read_2[1], Read_2[2]}), .Mux1({Read_1[0], Read_1[1], Read_1[2]}));
  Decoder #(.select(2), .disabled(0)) decoder_1 (
    .out0(decoder_1_out0), .out1(decoder_1_out1), .out2(decoder_1_out2), .out3(decoder_1_out3),
    .sel({Select_Registro[3], Select_Registro[4]}), .en(and_1_out));
  _8x32 u_8x32_2 (
    .Enable(decoder_1_out1), .Selec_Salida({Select_Registro[0], Select_Registro[1], Select_Registro[2]}),
    .Clock(Clock), .in_4(demultiplexer_1_out1), .Salida_1(n8x32_2_salida_1), .out_8(n8x32_2_out_8),
    .Mux2({Read_2[0], Read_2[1], Read_2[2]}), .Mux1({Read_1[0], Read_1[1], Read_1[2]}));
  _8x32 u_8x32_3 (
    .Enable(decoder_1_out2), .Selec_Salida({Select_Registro[0], Select_Registro[1], Select_Registro[2]}),
    .Clock(Clock), .in_4(demultiplexer_1_out2), .Salida_1(n8x32_3_salida_1), .out_8(n8x32_3_out_8),
    .Mux2({Read_2[0], Read_2[1], Read_2[2]}), .Mux1({Read_1[0], Read_1[1], Read_1[2]}));
  _8x32 u_8x32_4 (
    .Enable(decoder_1_out3), .Selec_Salida({Select_Registro[0], Select_Registro[1], Select_Registro[2]}),
    .Clock(Clock), .in_4(demultiplexer_1_out3), .Salida_1(n8x32_4_salida_1), .out_8(n8x32_4_out_8),
    .Mux2({Read_2[0], Read_2[1], Read_2[2]}), .Mux1({Read_1[0], Read_1[1], Read_1[2]}));
  Multiplexer #(.select(2), .width(32), .enable("false")) multiplexer_1 (
    .in0(n8x32_1_salida_1), .in1(n8x32_2_salida_1), .in2(n8x32_3_salida_1), .in3(n8x32_4_salida_1),
    .out(out_7), .sel({Read_1[3], Read_1[4]}));
  Multiplexer #(.select(2), .width(32), .enable("false")) multiplexer_2 (
    .in0(n8x32_1_out_8), .in1(n8x32_2_out_8), .in2(n8x32_3_out_8), .in3(n8x32_4_out_8), .out(out_8),
    .sel({Read_2[3], Read_2[4]}));
endmodule
