// Logisim project i7.circ as structural Verilog: 9 circuits, main circuit main
module main (
);

  wire alu_1_zero, and_1_out, clock_1_out, unidaddecontrol_1_alusrc, unidaddecontrol_1_branch,
       unidaddecontrol_1_jump, unidaddecontrol_1_memread, unidaddecontrol_1_memtoreg,
       unidaddecontrol_1_memwrite, unidaddecontrol_1_regdst, unidaddecontrol_1_regwrite;
  wire [1:0] unidaddecontrol_1_aluop;
  wire [3:0] alucontrol_1_out_3;
  wire [4:0] multiplexer_1_out;
  wire [27:0] n26_a28_1_out_2;
  wire [31:0] adder_1_out, adder_2_out, alu_1_out_5, banco_1_out_7, banco_1_out_8, bit_extender_1_out,
       memoria_1_readed_data, memoriadeinstrucciones_1_out_3, memoriadeinstrucciones_1_out_4,
       multiplexer_2_out, multiplexer_3_out, multiplexer_5_out, shifter_1_out, Tunelsito;

  Clock clock_1 (.out(clock_1_out));
  MemoriaDeInstrucciones memoriadeinstrucciones_1 (
    .in_1(Tunelsito), .out_4(memoriadeinstrucciones_1_out_4), .in_2(clock_1_out),
    .out_3(memoriadeinstrucciones_1_out_3));
  Adder #(.width(32)) adder_1 (.a(memoriadeinstrucciones_1_out_3), .b(32'h4), .out(adder_1_out));  // open: cin, cout
  _26_a28 u_26_a28_1 (.in_1(memoriadeinstrucciones_1_out_4), .out_2(n26_a28_1_out_2));
  UnidadDeCOntrol unidaddecontrol_1 (
    .Opcode(memoriadeinstrucciones_1_out_4[31:26]), .RegDst(unidaddecontrol_1_regdst),
    .Jump(unidaddecontrol_1_jump), .Branch(unidaddecontrol_1_branch), .MemRead(unidaddecontrol_1_memread),
    .MemToReg(unidaddecontrol_1_memtoreg), .AluOp(unidaddecontrol_1_aluop),
    .MemWrite(unidaddecontrol_1_memwrite), .AluSrc(unidaddecontrol_1_alusrc),
    .RegWrite(unidaddecontrol_1_regwrite));
  Multiplexer #(.width(5), .enable("false")) multiplexer_1 (
    .in0(memoriadeinstrucciones_1_out_4[20:16]), .in1(memoriadeinstrucciones_1_out_4[15:11]),
    .out(multiplexer_1_out), .sel(unidaddecontrol_1_regdst));
  assign bit_extender_1_out = {{16{memoriadeinstrucciones_1_out_4[15]}}, memoriadeinstrucciones_1_out_4[15:0]};  // Bit_Extender bit_extender_1
  Banco banco_1 (
    .Enable(unidaddecontrol_1_regwrite), .Clock(clock_1_out), .Read_1(memoriadeinstrucciones_1_out_4[25:21]),
    .Read_2(memoriadeinstrucciones_1_out_4[20:16]), .Select_Registro(multiplexer_1_out),
    .in_6(multiplexer_5_out), .out_7(banco_1_out_7), .out_8(banco_1_out_8));
  Shifter #(.width(32)) shifter_1 (.in(bit_extender_1_out), .\dist (5'b00010), .out(shifter_1_out));
  Multiplexer #(.width(32), .enable("false")) multiplexer_2 (
    .in0(banco_1_out_8), .in1(bit_extender_1_out), .out(multiplexer_2_out), .sel(unidaddecontrol_1_alusrc));
  AluControl alucontrol_1 (
    .Function(memoriadeinstrucciones_1_out_4[5:0]), .AluOp(unidaddecontrol_1_aluop),
    .out_3(alucontrol_1_out_3));
  Adder #(.width(32)) adder_2 (.a(adder_1_out), .b(shifter_1_out), .out(adder_2_out));  // open: cin, cout
  ALu alu_1 (
    .in_1(banco_1_out_7), .in_2(multiplexer_2_out), .Zero(alu_1_zero), .in_3(alucontrol_1_out_3),
    .out_5(alu_1_out_5));
  Multiplexer #(.width(32), .enable("false")) multiplexer_3 (
    .in0(adder_1_out), .in1(adder_2_out), .out(multiplexer_3_out), .sel(and_1_out));
  and and_1 (and_1_out, unidaddecontrol_1_branch, alu_1_zero);
  memoria memoria_1 (
    .Memory_Address(alu_1_out_5), .Data(banco_1_out_8), .Readed_Data(memoria_1_readed_data),
    .MemWrite(unidaddecontrol_1_memwrite), .CLK(clock_1_out), .MemRead(unidaddecontrol_1_memread));
  Multiplexer #(.width(32), .enable("false")) multiplexer_4 (
    .in0(multiplexer_3_out), .in1({adder_1_out[31:28], n26_a28_1_out_2}), .out(Tunelsito),
    .sel(unidaddecontrol_1_jump));
  Multiplexer #(.width(32), .enable("false")) multiplexer_5 (
    .in0(alu_1_out_5), .in1(memoria_1_readed_data), .out(multiplexer_5_out), .sel(unidaddecontrol_1_memtoreg));
endmodule

// Alu
module ALu (
  input  [31:0] in_1,
  input  [31:0] in_2,
  input  [3:0] in_3,
  output Zero,
  output [31:0] out_5
);

  wire comparator_1_eq, comparator_1_lt, zeroalu_1_out_2;
  wire [31:0] adder_1_out, and_1_out, bit_extender_1_out, nor_1_out, or_2_out, subtractor_1_out;

  Comparator #(.width(32)) comparator_1 (.a(in_1), .b(in_2), .eq(comparator_1_eq), .lt(comparator_1_lt));  // open: gt
  or or_1 (Zero, comparator_1_eq, zeroalu_1_out_2);
  Adder #(.width(32)) adder_1 (.a(in_1), .b(in_2), .out(adder_1_out));  // open: cin, cout
  Subtractor #(.width(32)) subtractor_1 (.a(in_1), .b(in_2), .out(subtractor_1_out));  // open: bin, bout
  assign bit_extender_1_out = {{31{1'b0}}, comparator_1_lt};  // Bit_Extender bit_extender_1
  assign and_1_out = in_1 & in_2;  // AND_Gate and_1, 32 bits wide
  assign or_2_out = in_1 | in_2;  // OR_Gate or_2, 32 bits wide
  assign nor_1_out = ~(in_1 | in_2);  // NOR_Gate nor_1, 32 bits wide
  Multiplexer #(.select(4), .width(32), .enable("false")) multiplexer_1 (
    .in0(and_1_out), .in1(or_2_out), .in2(adder_1_out), .in6(subtractor_1_out), .in7(bit_extender_1_out),
    .in12(nor_1_out), .out(out_5), .sel(in_3));  // open: in3, in4, in5, in8, in9, in10, in11, in13, in14, in15
  ZeroAlu zeroalu_1 (.in_1(out_5), .out_2(zeroalu_1_out_2));
endmodule

// U.C
module UnidadDeCOntrol (
  input  [5:0] Opcode,
  output RegDst,
  output Jump,
  output Branch,
  output MemRead,
  output MemToReg,
  output [1:0] AluOp,
  output MemWrite,
  output AluSrc,
  output RegWrite
);

  ROM #(.addrWidth(6), .dataWidth(10)) rom_1 (
    .addr(Opcode), .data({RegWrite, AluSrc, MemWrite, AluOp, MemToReg, MemRead, Branch, Jump, RegDst}),
    .sel(1'b1));

  // Notes on the sheet:
  //   contents of rom_1 (hex, n*v repeats v):
  //   241 0 2 0 24 0 0 0 300 26*0 318 7*0 180
endmodule

// M.I
module MemoriaDeInstrucciones (
  input  [31:0] in_1,
  input  in_2,
  output [31:0] out_3,
  output [31:0] out_4
);

  wire [31:0] shifter_1_out;

  Register #(.width(32)) register_1 (.D(in_1), .Q(out_3), .clk(in_2));  // open: en, clr
  Shifter #(.width(32), .shift("lr")) shifter_1 (.in(out_3), .\dist (5'b00010), .out(shifter_1_out));
  ROM #(.addrWidth(24), .dataWidth(32)) rom_1 (.addr(shifter_1_out[23:0]), .data(out_4), .sel(1'b1));

  // Notes on the sheet:
  //   contents of rom_1 (hex, n*v repeats v):
  //   20100000 20110014 20080000 20090001 20120000 ae480000 22100001 22520004 ae490000 22100001 22520004
  //   12110007 8e48fff8 8e49fffc 1095820 ae4b0000 22100001 22520004 800000b
endmodule

// AluC
module AluControl (
  input  [5:0] Function,
  input  [1:0] AluOp,
  output [3:0] out_3
);

  wire [3:0] rom_1_data;

  ROM #(.addrWidth(6), .dataWidth(4)) rom_1 (.addr(Function), .data(rom_1_data));  // open: sel
  Multiplexer #(.select(2), .width(4), .enable("false")) multiplexer_1 (
    .in0(4'b0010), .in1(4'b0110), .in2(rom_1_data), .out(out_3), .sel(AluOp));  // open: in3

  // Notes on the sheet:
  //   contents of rom_1 (hex, n*v repeats v):
  //   32*0 2 0 6 0 0 1 0 c 0 0 7
endmodule

// Data
module memoria (
  input  [31:0] Memory_Address,
  input  [31:0] Data,
  input  MemRead,
  input  MemWrite,
  input  CLK,
  output [31:0] Readed_Data
);

  wire [31:0] shifter_1_out;

  Shifter #(.width(32), .shift("lr")) shifter_1 (.in(Memory_Address), .\dist (5'b00010), .out(shifter_1_out));
  RAM #(.addrWidth(24), .dataWidth(32), .bus("separate")) ram_1 (
    .addr(shifter_1_out[23:0]), .din(Data), .data(Readed_Data), .str(MemWrite), .clk(CLK), .ld(MemRead));  // open: sel, clr
  // Probe on Readed_Data
endmodule

module \DirecciónSalto  (
  input  [31:0] PC_4,
  input  [25:0] TargetAddress,
  output [31:0] AddressJump
);


  assign AddressJump = {PC_4[31:28], TargetAddress, 2'b00};
endmodule

module _26_a28 (
  input  [31:0] in_1,
  output [27:0] out_2
);

  wire [27:0] bit_extender_1_out;

  assign bit_extender_1_out = {{2{1'b0}}, in_1[25:0]};  // Bit_Extender bit_extender_1
  Shifter #(.width(28)) shifter_1 (.in(bit_extender_1_out), .\dist (5'b00010), .out(out_2));
endmodule

module ZeroAlu (
  input  [31:0] in_1,
  output out_2
);

  nor nor_1 (out_2, in_1[0], in_1[1], in_1[2], in_1[3], in_1[4], in_1[5], in_1[6], in_1[7], in_1[8], in_1[9], in_1[10], in_1[11], in_1[12], in_1[13], in_1[14], in_1[15], in_1[16], in_1[17], in_1[18], in_1[19], in_1[20], in_1[21], in_1[22], in_1[23], in_1[24], in_1[25], in_1[26], in_1[27], in_1[28], in_1[29], in_1[30], in_1[31]);
endmodule
